// Logisim project bonkpu.circ as structural Verilog: 1 circuit, main circuit main
module main (
);

  wire CLK, dipswitch_1_sw2, not_1_out;
  wire [2:0] FLAGS, nor_1_out;
  wire [3:0] MICROSTEP_q;
  wire [7:0] A_REG_q, adder_1_out, B_REG_q, controlled_buffer_1_out, dipswitch_2_sw8, microcode_b_data,
       microcode_c_data, multiplexer_1_out, OP_REG_q, xor_1_out;
  wire [23:16] microcode_a_data;

  Button button_1 (.out(CLK));
  not not_1 (not_1_out, CLK);
  Counter #(.max('hf), .width(4)) MICROSTEP (
    .load(microcode_c_data[0]), .clk(not_1_out), .D(4'b0000), .Q(MICROSTEP_q));  // open: clr, up, count, carry
  Register OP_REG (.D(controlled_buffer_1_out), .en(microcode_a_data[18]), .clk(CLK), .Q(OP_REG_q));  // open: clr
  ROM #(.addrWidth(15)) microcode_a (.addr({FLAGS, OP_REG_q, MICROSTEP_q}), .data(microcode_a_data));
  DipSwitch #(.number(2)) dipswitch_1 (.sw2(dipswitch_1_sw2));  // open: sw1
  ROM #(.addrWidth(15)) microcode_b (.addr({FLAGS, OP_REG_q, MICROSTEP_q}), .data(microcode_b_data));
  assign controlled_buffer_1_out = dipswitch_1_sw2 ? dipswitch_2_sw8 : 8'bz;  // Controlled_Buffer controlled_buffer_1
  DipSwitch dipswitch_2 (
    .sw1(dipswitch_2_sw8[7]), .sw2(dipswitch_2_sw8[6]), .sw3(dipswitch_2_sw8[5]), .sw4(dipswitch_2_sw8[4]),
    .sw5(dipswitch_2_sw8[3]), .sw6(dipswitch_2_sw8[2]), .sw7(dipswitch_2_sw8[1]), .sw8(dipswitch_2_sw8[0]));
  Pull_Resistor pull_resistor_1 (.node(controlled_buffer_1_out));
  LedBar ledbar_1 (
    .led0(controlled_buffer_1_out[7]), .led1(controlled_buffer_1_out[6]), .led2(controlled_buffer_1_out[5]),
    .led3(controlled_buffer_1_out[4]), .led4(controlled_buffer_1_out[3]), .led5(controlled_buffer_1_out[2]),
    .led6(controlled_buffer_1_out[1]), .led7(controlled_buffer_1_out[0]));
  Register A_REG (.D(controlled_buffer_1_out), .en(microcode_a_data[16]), .clk(CLK), .Q(A_REG_q));  // open: clr
  assign controlled_buffer_1_out = microcode_b_data[4] ? adder_1_out : 8'bz;  // Controlled_Buffer EO_GATE
  Register B_REG (.D(controlled_buffer_1_out), .en(microcode_b_data[6]), .clk(CLK), .Q(B_REG_q));  // open: clr
  assign controlled_buffer_1_out = microcode_b_data[5] ? B_REG_q : 8'bz;  // Controlled_Buffer B_GATE
  ROM #(.addrWidth(15)) microcode_c (.addr({FLAGS, OP_REG_q, MICROSTEP_q}), .data(microcode_c_data));
  LedBar #(.matrixcols(24)) ledbar_2 (
    .led0(microcode_a_data[23]), .led1(microcode_a_data[22]), .led2(microcode_a_data[21]),
    .led3(microcode_a_data[20]), .led4(microcode_a_data[19]), .led5(microcode_a_data[18]),
    .led6(microcode_a_data[17]), .led7(microcode_a_data[16]), .led8(microcode_b_data[7]),
    .led9(microcode_b_data[6]), .led10(microcode_b_data[5]), .led11(microcode_b_data[4]),
    .led12(microcode_b_data[3]), .led13(microcode_b_data[2]), .led14(microcode_b_data[1]),
    .led15(microcode_b_data[0]), .led16(microcode_c_data[7]), .led17(microcode_c_data[6]),
    .led18(microcode_c_data[5]), .led19(microcode_c_data[4]), .led20(microcode_c_data[3]),
    .led21(microcode_c_data[2]), .led22(microcode_c_data[1]), .led23(microcode_c_data[0]));
  assign controlled_buffer_1_out = microcode_b_data[7] ? A_REG_q : 8'bz;  // Controlled_Buffer controlled_buffer_2
  Multiplexer #(.width(8)) multiplexer_1 (
    .in0({8{1'b0}}), .in1({8{1'b1}}), .out(multiplexer_1_out), .sel(microcode_b_data[3]));
  assign xor_1_out = multiplexer_1_out ^ B_REG_q;  // XOR_Gate xor_1, 8 bits wide
  Adder adder_1 (.a(A_REG_q), .b(xor_1_out), .out(adder_1_out), .cin(microcode_b_data[3]), .cout(nor_1_out[2]));
  // Probe on adder_1_out
  // Probe on adder_1_out
  nor nor_1 (nor_1_out[0], adder_1_out[0], adder_1_out[1], adder_1_out[2], adder_1_out[3], adder_1_out[4], adder_1_out[5], adder_1_out[6], adder_1_out[7]);
  Register #(.width(3)) FLAG_REG (
    .D({nor_1_out[2], adder_1_out[7], nor_1_out[0]}), .en(microcode_b_data[2]), .clk(CLK), .Q(FLAGS));  // open: clr
  LedBar #(.matrixcols(3)) ledbar_3 (.led0(FLAGS[2]), .led1(FLAGS[1]), .led2(FLAGS[0]));

  // Notes on the sheet:
  //   contents of microcode_a (hex, n*v repeats v):
  //   40 20 c 13*0 40 20 c 0 40 20 9 9*0 40 20 c 0 40 20 8 1 8*0 40 20 c 0 40 20 8 1 8*0 40 20 c 0 40 20 8
  //   40 20 8 6*0 40 20 c 13*0 40 20 c 0 40 20 8 40 20 8 6*0 40 20 c 13*0 40 20 c 0 40 20 8 40 20 8 6*0 40
  //   20 c 13*0 40 20 c 0 40 20 8 40 20 8 6*0 40 20 c 0 80 11*0 40 20 c 13*0 40 20 c 13*0 40 20 c 13*0 40
  //   20 c 13*0 40 20 c 13*0 40 20 c 13*0 40 20 c 13*0 40 20 c 13*0 40 20 c 13*0 40 20 c 13*0 40 20 c 13*0
  //   40 20 c 13*0 40 20 c 13*0 40 20 c 13*0 40 20 c 13*0 40 20 c 13*0 40 20 c 13*0 40 20 c 13*0 40 20 c
  //   13*0 40 20 c 13*0 40 20 c 13*0 40 20 c 13*0 40 20 c 13*0 40 20 c 13*0 40 20 c 13*0 40 20 c 13*0 40
  //   20 c 13*0 40 20 c 13*0 40 20 c 13*0 40 20 c 13*0 40 20 c 13*0 40 20 c 13*0 40 20 c 13*0 40 20 c 13*0
  //   40 20 c 13*0 40 20 c 13*0 40 20 c 13*0 40 20 c 13*0 40 20 c 13*0 40 20 c 13*0 40 20 c 13*0 40 20 c
  //   13*0 40 20 c 13*0 40 20 c 13*0 40 20 c 13*0 40 20 c 13*0 40 20 c 13*0 40 20 c 13*0 40 20 c 13*0 40
  //   20 c 13*0 40 20 c 13*0 40 20 c 13*0 40 20 c 13*0 40 20 c 13*0 40 20 c 13*0 40 20 c 13*0 40 20 c 13*0
  //   40 20 c 13*0 40 20 c 13*0 40 20 c 13*0 40 20 c 13*0 40 20 c 13*0 40 20 c 13*0 40 20 c 13*0 40 20 c
  //   13*0 40 20 c 13*0 40 20 c 13*0 40 20 c 13*0 40 20 c 13*0 40 20 c 13*0 40 20 c 13*0 40 20 c 13*0 40
  //   20 c 13*0 40 20 c 13*0 40 20 c 13*0 40 20 c 13*0 40 20 c 13*0 40 20 c 13*0 40 20 c 13*0 40 20 c 13*0
  //   40 20 c 13*0 40 20 c 13*0 40 20 c 13*0 40 20 c 13*0 40 20 c 13*0 40 20 c 13*0 40 20 c 13*0 40 20 c
  //   13*0 40 20 c 13*0 40 20 c 13*0 40 20 c 13*0 40 20 c 13*0 40 20 c 13*0 40 20 c 13*0 40 20 c 13*0 40
  //   20 c 13*0 40 20 c 13*0 40 20 c 13*0 40 20 c 13*0 40 20 c 13*0 40 20 c 13*0 40 20 c 13*0 40 20 c 13*0
  //   40 20 c 13*0 40 20 c 13*0 40 20 c 13*0 40 20 c 13*0 40 20 c 13*0 40 20 c 13*0 40 20 c 13*0 40 20 c
  //   13*0 40 20 c 13*0 40 20 c 13*0 40 20 c 13*0 40 20 c 13*0 40 20 c 13*0 40 20 c 13*0 40 20 c 13*0 40
  //   20 c 13*0 40 20 c 13*0 40 20 c 13*0 40 20 c 13*0 40 20 c 13*0 40 20 c 13*0 40 20 c 13*0 40 20 c 13*0
  //   40 20 c 13*0 40 20 c 13*0 40 20 c 13*0 40 20 c 13*0 40 20 c 13*0 40 20 c 13*0 40 20 c 13*0 40 20 c
  //   13*0 40 20 c 13*0 40 20 c 13*0 40 20 c 13*0 40 20 c 13*0 40 20 c 13*0 40 20 c 13*0 40 20 c 13*0 40
  //   20 c 13*0 40 20 c 13*0 40 20 c 13*0 40 20 c 13*0 40 20 c 13*0 40 20 c 13*0 40 20 c 13*0 40 20 c 13*0
  //   40 20 c 13*0 40 20 c 13*0 40 20 c 13*0 40 20 c 13*0 40 20 c 13*0 40 20 c 13*0 40 20 c 13*0 40 20 c
  //   13*0 40 20 c 13*0 40 20 c 13*0 40 20 c 13*0 40 20 c 13*0 40 20 c 13*0 40 20 c 13*0 40 20 c 13*0 40
  //   20 c 13*0 40 20 c 13*0 40 20 c 13*0 40 20 c 13*0 40 20 c 13*0 40 20 c 13*0 40 20 c 13*0 40 20 c 13*0
  //   40 20 c 13*0 40 20 c 13*0 40 20 c 13*0 40 20 c 13*0 40 20 c 13*0 40 20 c 13*0 40 20 c 13*0 40 20 c
  //   13*0 40 20 c 13*0 40 20 c 13*0 40 20 c 13*0 40 20 c 13*0 40 20 c 13*0 40 20 c 13*0 40 20 c 13*0 40
  //   20 c 13*0 40 20 c 13*0 40 20 c 13*0 40 20 c 13*0 40 20 c 13*0 40 20 c 13*0 40 20 c 13*0 40 20 c 13*0
  //   40 20 c 13*0 40 20 c 13*0 40 20 c 13*0 40 20 c 13*0 40 20 c 13*0 40 20 c 13*0 40 20 c 13*0 40 20 c
  //   13*0 40 20 c 13*0 40 20 c 13*0 40 20 c 13*0 40 20 c 13*0 40 20 c 13*0 40 20 c 13*0 40 20 c 13*0 40
  //   20 c 13*0 40 20 c 13*0 40 20 c 13*0 40 20 c 13*0 40 20 c 13*0 40 20 c 13*0 40 20 c 13*0 40 20 c 13*0
  //   40 20 c 13*0 40 20 c 13*0 40 20 c 13*0 40 20 c 13*0 40 20 c 13*0 40 20 c 13*0 40 20 c 13*0 40 20 c
  //   13*0 40 20 c 13*0 40 20 c 13*0 40 20 c 13*0 40 20 c 13*0 40 20 c 13*0 40 20 c 13*0 40 20 c 13*0 40
  //   20 c 13*0 40 20 c 13*0 40 20 c 13*0 40 20 c 13*0 40 20 c 13*0 40 20 c 13*0 40 20 c 13*0 40 20 c 13*0
  //   40 20 c 13*0 40 20 c 13*0 40 20 c 13*0 40 20 c 13*0 40 20 c 0 40 20 9 9*0 40 20 c 0 40 20 8 1 8*0 40
  //   20 c 0 40 20 8 1 8*0 40 20 c 0 40 20 8 40 20 8 6*0 40 20 c 0 40 20 8 40 20 8 6*0 40 20 c 13*0 40 20
  //   c 13*0 40 20 c 0 40 20 8 40 20 8 6*0 40 20 c 13*0 40 20 c 0 40 20 8 40 20 8 6*0 40 20 c 0 80 11*0 40
  //   20 c 13*0 40 20 c 13*0 40 20 c 13*0 40 20 c 13*0 40 20 c 13*0 40 20 c 13*0 40 20 c 13*0 40 20 c 13*0
  //   40 20 c 13*0 40 20 c 13*0 40 20 c 13*0 40 20 c 13*0 40 20 c 13*0 40 20 c 13*0 40 20 c 13*0 40 20 c
  //   13*0 40 20 c 13*0 40 20 c 13*0 40 20 c 13*0 40 20 c 13*0 40 20 c 13*0 40 20 c 13*0 40 20 c 13*0 40
  //   20 c 1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
  //   contents of microcode_b (hex, n*v repeats v):
  //   0 0 2 2 14*0 2 2 1 0 2 11*0 2 2 1 0 42 14 10*0 2 2 1 0 42 1c 10*0 2 2 1 0 42 1 0 2 20 7*0 4*2 12*0 2
  //   2 1 0 42 1 0 2 20 7*0 4*2 12*0 2 2 1 0 42 1 0 2 20 7*0 4*2 12*0 2 2 1 0 42 1 0 2 20 7*0 2 2 14*0 2 2
  //   14*0 2 2 14*0 2 2 14*0 2 2 14*0 2 2 14*0 2 2 14*0 2 2 14*0 2 2 14*0 2 2 14*0 2 2 14*0 2 2 14*0 2 2
  //   14*0 2 2 14*0 2 2 14*0 2 2 14*0 2 2 14*0 2 2 14*0 2 2 14*0 2 2 14*0 2 2 14*0 2 2 14*0 2 2 14*0 2 2
  //   14*0 2 2 14*0 2 2 14*0 2 2 14*0 2 2 14*0 2 2 14*0 2 2 14*0 2 2 14*0 2 2 14*0 2 2 14*0 2 2 14*0 2 2
  //   14*0 2 2 14*0 2 2 14*0 2 2 14*0 2 2 14*0 2 2 14*0 2 2 14*0 2 2 14*0 2 2 14*0 2 2 14*0 2 2 14*0 2 2
  //   14*0 2 2 14*0 2 2 14*0 2 2 14*0 2 2 14*0 2 2 14*0 2 2 14*0 2 2 14*0 2 2 14*0 2 2 14*0 2 2 14*0 2 2
  //   14*0 2 2 14*0 2 2 14*0 2 2 14*0 2 2 14*0 2 2 14*0 2 2 14*0 2 2 14*0 2 2 14*0 2 2 14*0 2 2 14*0 2 2
  //   14*0 2 2 14*0 2 2 14*0 2 2 14*0 2 2 14*0 2 2 14*0 2 2 14*0 2 2 14*0 2 2 14*0 2 2 14*0 2 2 14*0 2 2
  //   14*0 2 2 14*0 2 2 14*0 2 2 14*0 2 2 14*0 2 2 14*0 2 2 14*0 2 2 14*0 2 2 14*0 2 2 14*0 2 2 14*0 2 2
  //   14*0 2 2 14*0 2 2 14*0 2 2 14*0 2 2 14*0 2 2 14*0 2 2 14*0 2 2 14*0 2 2 14*0 2 2 14*0 2 2 14*0 2 2
  //   14*0 2 2 14*0 2 2 14*0 2 2 14*0 2 2 14*0 2 2 14*0 2 2 14*0 2 2 14*0 2 2 14*0 2 2 14*0 2 2 14*0 2 2
  //   14*0 2 2 14*0 2 2 14*0 2 2 14*0 2 2 14*0 2 2 14*0 2 2 14*0 2 2 14*0 2 2 14*0 2 2 14*0 2 2 14*0 2 2
  //   14*0 2 2 14*0 2 2 14*0 2 2 14*0 2 2 14*0 2 2 14*0 2 2 14*0 2 2 14*0 2 2 14*0 2 2 14*0 2 2 14*0 2 2
  //   14*0 2 2 14*0 2 2 14*0 2 2 14*0 2 2 14*0 2 2 14*0 2 2 14*0 2 2 14*0 2 2 14*0 2 2 14*0 2 2 14*0 2 2
  //   14*0 2 2 14*0 2 2 14*0 2 2 14*0 2 2 14*0 2 2 14*0 2 2 14*0 2 2 14*0 2 2 14*0 2 2 14*0 2 2 14*0 2 2
  //   14*0 2 2 14*0 2 2 14*0 2 2 14*0 2 2 14*0 2 2 14*0 2 2 14*0 2 2 14*0 2 2 14*0 2 2 14*0 2 2 14*0 2 2
  //   14*0 2 2 14*0 2 2 14*0 2 2 14*0 2 2 14*0 2 2 14*0 2 2 14*0 2 2 14*0 2 2 14*0 2 2 14*0 2 2 14*0 2 2
  //   14*0 2 2 14*0 2 2 14*0 2 2 14*0 2 2 14*0 2 2 14*0 2 2 14*0 2 2 14*0 2 2 14*0 2 2 14*0 2 2 14*0 2 2
  //   14*0 2 2 14*0 2 2 14*0 2 2 14*0 2 2 14*0 2 2 14*0 2 2 14*0 2 2 14*0 2 2 14*0 2 2 14*0 2 2 14*0 2 2
  //   14*0 2 2 14*0 2 2 14*0 2 2 14*0 2 2 14*0 2 2 14*0 2 2 14*0 2 2 14*0 2 2 14*0 2 2 14*0 2 2 14*0 2 2
  //   14*0 2 2 14*0 2 2 14*0 2 2 14*0 2 2 14*0 2 2 14*0 2 2 14*0 2 2 14*0 2 2 14*0 2 2 14*0 2 2 14*0 2 2
  //   14*0 2 2 14*0 2 2 14*0 2 2 14*0 2 2 14*0 2 2 14*0 2 2 14*0 2 2 14*0 2 2 14*0 2 2 14*0 2 2 14*0 2 2
  //   14*0 2 2 14*0 2 2 14*0 2 2 14*0 2 2 14*0 2 2 14*0 2 2 14*0 2 2 14*0 2 2 14*0 2 2 14*0 2 2 14*0 2 2
  //   14*0 2 2 14*0 2 2 14*0 2 2 1 0 2 11*0 2 2 1 0 42 14 10*0 2 2 1 0 42 1c 10*0 2 2 1 0 42 1 0 2 20 7*0
  //   2 2 1 0 42 1 0 2 20 7*0 4*2 12*0 4*2 12*0 2 2 1 0 42 1 0 2 20 7*0 4*2 12*0 2 2 1 0 42 1 0 2 20 7*0 2
  //   2 14*0 2 2 14*0 2 2 14*0 2 2 14*0 2 2 14*0 2 2 14*0 2 2 14*0 2 2 14*0 2 2 14*0 2 2 14*0 2 2 14*0 2 2
  //   14*0 2 2 14*0 2 2 14*0 2 2 14*0 2 2 14*0 2 2 14*0 2 2 14*0 2 2 14*0 2 2 14*0 2 2 14*0 2 2 14*0 2 2
  //   14*0 2 2 14*0 2 2 14*0 2 2 14*0 2 2 14*0 2 2 14*0 2 2 14*0 2 2 14*0 2 2 14*0 2 2 14*0 2 2 14*0 2 2
  //   14*0 2 2 14*0 2 2 14*0 2 2 14*0 2 2 14*0 2 2 14*0 2 2 14*0 2 2 14*0 2 2 14*0 2 2 14*0 2 2 14*0 2 2
  //   14*0 2 2 14*0 2 2 14*0 2 2 14*0 2 2 14*0 2 2 14*0 2 2 14*0 2 2 14*0 2 2 14*0 2 2 14*0 2 2 14*0 2 2
  //   14*0 2 2 14*0 2 2 14*0 2 2 14*0 2 2 14*0 2 2 14*0 2 2 14*0 2 2 14*0 2 2 14*0 2 2 14*0 2 2 14*0 2 2
  //   14*0 2 2 14*0 2 2 14*0 2 2 14*0 2 2 14*0 2 2 14*0 2 2 14*0 2 2 14*0 2 2 14*0 2 2 14*0 2 2 14*0 2 2
  //   14*0 2 2 14*0 2 2 14*0 2 2 14*0 2 2 14*0 2 2 14*0 2 2 14*0 2 2 14*0 2 2 14*0 2 2 14*0 2 2 14*0 2 2
  //   14*0 2 2 14*0 2 2 14*0 2 2 14*0 2 2 14*0 2 2 14*0 2 2 14*0 2 2 14*0 2 2 14*0 2 2 14*0 2 2 14*0 2 2
  //   14*0 2 2 14*0 2 2 14*0 2 2 14*0 2 2 14*0 2 2 14*0 2 2 14*0 2 2 14*0 2 2 14*0 2 2 14*0 2 2 14*0 2 2
  //   14*0 2 2 14*0 2 2 14*0 2 2 14*0 2 2 14*0 2 2 14*0 2 2 14*0 2 2 14*0 2 2 14*0 2 2 14*0 2 2 14*0 2 2
  //   14*0 2 2 14*0 2 2 14*0 2 2 14*0 2 2 14*0 2 2 14*0 2 2 14*0 2 2 14*0 2 2 14*0 2 2 14*0 2 2 14*0 2 2
  //   14*0 2 2 14*0 2 2 14*0 2 2 14*0 2 2 14*0 2 2 14*0 2 2 14*0 2 2 14*0 2 2 14*0 2 2 14*0 2 2 14*0 2 2
  //   14*0 2 2 14*0 2 2 14*0 2 2 14*0 2 2 14*0 2 2 14*0 2 2 14*0 2 2 14*0 2 2 14*0 2 2 14*0 2 2 14*0 2 2
  //   14*0 2 2 14*0 2 2 14*0 2 2 14*0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
  //   contents of microcode_c (hex, n*v repeats v):
  //   40 20 0 1 12*0 40 20 0 0 0 80 1 9*0 40 20 0 0 0 80 0 1 8*0 40 20 0 0 0 80 0 1 8*0 40 20 0 0 0 80 0 0
  //   80 40 21 5*0 40 20 0 0 0 1 10*0 40 20 0 0 0 80 0 0 80 40 21 5*0 40 20 0 0 0 1 10*0 40 20 0 0 0 80 0
  //   0 80 40 21 5*0 40 20 0 0 0 1 10*0 40 20 0 0 0 80 0 0 80 40 21 5*0 40 20 0 0 1 11*0 40 20 0 1 12*0 40
  //   20 0 1 12*0 40 20 0 1 12*0 40 20 0 1 12*0 40 20 0 1 12*0 40 20 0 1 12*0 40 20 0 1 12*0 40 20 0 1
  //   12*0 40 20 0 1 12*0 40 20 0 1 12*0 40 20 0 1 12*0 40 20 0 1 12*0 40 20 0 1 12*0 40 20 0 1 12*0 40 20
  //   0 1 12*0 40 20 0 1 12*0 40 20 0 1 12*0 40 20 0 1 12*0 40 20 0 1 12*0 40 20 0 1 12*0 40 20 0 1 12*0
  //   40 20 0 1 12*0 40 20 0 1 12*0 40 20 0 1 12*0 40 20 0 1 12*0 40 20 0 1 12*0 40 20 0 1 12*0 40 20 0 1
  //   12*0 40 20 0 1 12*0 40 20 0 1 12*0 40 20 0 1 12*0 40 20 0 1 12*0 40 20 0 1 12*0 40 20 0 1 12*0 40 20
  //   0 1 12*0 40 20 0 1 12*0 40 20 0 1 12*0 40 20 0 1 12*0 40 20 0 1 12*0 40 20 0 1 12*0 40 20 0 1 12*0
  //   40 20 0 1 12*0 40 20 0 1 12*0 40 20 0 1 12*0 40 20 0 1 12*0 40 20 0 1 12*0 40 20 0 1 12*0 40 20 0 1
  //   12*0 40 20 0 1 12*0 40 20 0 1 12*0 40 20 0 1 12*0 40 20 0 1 12*0 40 20 0 1 12*0 40 20 0 1 12*0 40 20
  //   0 1 12*0 40 20 0 1 12*0 40 20 0 1 12*0 40 20 0 1 12*0 40 20 0 1 12*0 40 20 0 1 12*0 40 20 0 1 12*0
  //   40 20 0 1 12*0 40 20 0 1 12*0 40 20 0 1 12*0 40 20 0 1 12*0 40 20 0 1 12*0 40 20 0 1 12*0 40 20 0 1
  //   12*0 40 20 0 1 12*0 40 20 0 1 12*0 40 20 0 1 12*0 40 20 0 1 12*0 40 20 0 1 12*0 40 20 0 1 12*0 40 20
  //   0 1 12*0 40 20 0 1 12*0 40 20 0 1 12*0 40 20 0 1 12*0 40 20 0 1 12*0 40 20 0 1 12*0 40 20 0 1 12*0
  //   40 20 0 1 12*0 40 20 0 1 12*0 40 20 0 1 12*0 40 20 0 1 12*0 40 20 0 1 12*0 40 20 0 1 12*0 40 20 0 1
  //   12*0 40 20 0 1 12*0 40 20 0 1 12*0 40 20 0 1 12*0 40 20 0 1 12*0 40 20 0 1 12*0 40 20 0 1 12*0 40 20
  //   0 1 12*0 40 20 0 1 12*0 40 20 0 1 12*0 40 20 0 1 12*0 40 20 0 1 12*0 40 20 0 1 12*0 40 20 0 1 12*0
  //   40 20 0 1 12*0 40 20 0 1 12*0 40 20 0 1 12*0 40 20 0 1 12*0 40 20 0 1 12*0 40 20 0 1 12*0 40 20 0 1
  //   12*0 40 20 0 1 12*0 40 20 0 1 12*0 40 20 0 1 12*0 40 20 0 1 12*0 40 20 0 1 12*0 40 20 0 1 12*0 40 20
  //   0 1 12*0 40 20 0 1 12*0 40 20 0 1 12*0 40 20 0 1 12*0 40 20 0 1 12*0 40 20 0 1 12*0 40 20 0 1 12*0
  //   40 20 0 1 12*0 40 20 0 1 12*0 40 20 0 1 12*0 40 20 0 1 12*0 40 20 0 1 12*0 40 20 0 1 12*0 40 20 0 1
  //   12*0 40 20 0 1 12*0 40 20 0 1 12*0 40 20 0 1 12*0 40 20 0 1 12*0 40 20 0 1 12*0 40 20 0 1 12*0 40 20
  //   0 1 12*0 40 20 0 1 12*0 40 20 0 1 12*0 40 20 0 1 12*0 40 20 0 1 12*0 40 20 0 1 12*0 40 20 0 1 12*0
  //   40 20 0 1 12*0 40 20 0 1 12*0 40 20 0 1 12*0 40 20 0 1 12*0 40 20 0 1 12*0 40 20 0 1 12*0 40 20 0 1
  //   12*0 40 20 0 1 12*0 40 20 0 1 12*0 40 20 0 1 12*0 40 20 0 1 12*0 40 20 0 1 12*0 40 20 0 1 12*0 40 20
  //   0 1 12*0 40 20 0 1 12*0 40 20 0 1 12*0 40 20 0 1 12*0 40 20 0 1 12*0 40 20 0 1 12*0 40 20 0 1 12*0
  //   40 20 0 1 12*0 40 20 0 1 12*0 40 20 0 1 12*0 40 20 0 1 12*0 40 20 0 1 12*0 40 20 0 1 12*0 40 20 0 1
  //   12*0 40 20 0 1 12*0 40 20 0 1 12*0 40 20 0 1 12*0 40 20 0 1 12*0 40 20 0 1 12*0 40 20 0 1 12*0 40 20
  //   0 1 12*0 40 20 0 1 12*0 40 20 0 1 12*0 40 20 0 1 12*0 40 20 0 1 12*0 40 20 0 1 12*0 40 20 0 1 12*0
  //   40 20 0 1 12*0 40 20 0 1 12*0 40 20 0 1 12*0 40 20 0 1 12*0 40 20 0 1 12*0 40 20 0 1 12*0 40 20 0 1
  //   12*0 40 20 0 1 12*0 40 20 0 1 12*0 40 20 0 1 12*0 40 20 0 1 12*0 40 20 0 1 12*0 40 20 0 1 12*0 40 20
  //   0 1 12*0 40 20 0 1 12*0 40 20 0 1 12*0 40 20 0 1 12*0 40 20 0 1 12*0 40 20 0 1 12*0 40 20 0 1 12*0
  //   40 20 0 1 12*0 40 20 0 1 12*0 40 20 0 1 12*0 40 20 0 1 12*0 40 20 0 1 12*0 40 20 0 1 12*0 40 20 0 1
  //   12*0 40 20 0 1 12*0 40 20 0 1 12*0 40 20 0 1 12*0 40 20 0 1 12*0 40 20 0 1 12*0 40 20 0 1 12*0 40 20
  //   0 1 12*0 40 20 0 1 12*0 40 20 0 1 12*0 40 20 0 1 12*0 40 20 0 1 12*0 40 20 0 1 12*0 40 20 0 1 12*0
  //   40 20 0 1 12*0 40 20 0 1 12*0 40 20 0 1 12*0 40 20 0 1 12*0 40 20 0 1 12*0 40 20 0 1 12*0 40 20 0 1
  //   12*0 40 20 0 1 12*0 40 20 0 1 12*0 40 20 0 1 12*0 40 20 0 1 12*0 40 20 0 1 12*0 40 20 0 1 12*0 40 20
  //   0 1 12*0 40 20 0 1 12*0 40 20 0 1 12*0 40 20 0 1 12*0 40 20 0 1 12*0 40 20 0 1 12*0 40 20 0 1 12*0
  //   40 20 0 1 12*0 40 20 0 1 12*0 40 20 0 1 12*0 40 20 0 1 12*0 40 20 0 0 0 80 1 9*0 40 20 0 0 0 80 0 1
  //   8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
endmodule
